# Fritzing sketch ESP8266-12E No.3 - Temprature & Fan & Servo (saved by Fritzing 0.9.3b)
breadboards: 1

parts:
  IC5 = Voltage Regulator [package=to220-igo]
  IC6 = Voltage Regulator [package=to220-igo]
  U4 = ESP8266 WiFi Module [part_number=ESP8266]
  S4 = Pushbutton [package="[THT]"]
  U5 = RELAY [package=OJ]
  U6 = RELAY [package=OJ]
  T1 = LM35 Temperature Sensor [package="TO92 [THT]"]  # not connected

nets:
  GND: IC5.GND, IC6.GND, U5.COIL1, U6.COIL1
  N1: IC5.IN, IC6.IN, U4.GND, S4.Pin_3, S4.Pin_4, U5.COIL2, U6.COIL2
  N2: IC5.OUT, U4.VCC, U4.CH_PD
  N3: U4.GPIO_0, U5.MAIN
  N4: U4.GPIO_2, U6.MAIN
  N5: U4.REST, S4.Pin_1, S4.Pin_2
