# Fritzing sketch SoilMoisture-SolenoidValve (saved by Fritzing 0.9.3b)
breadboards: 1

parts:
  IC3 = Voltage Regulator [package=to220-igo]
  IC4 = Voltage Regulator [package=to220-igo]
  U2 = ESP8266 WiFi Module [part_number=ESP8266]
  S3 = Pushbutton [package="[THT]"]
  Part1 = Soil Moisture Sensor  # not connected
  U3 = RELAY [package=OJ]

nets:
  GND: IC3.GND, IC4.GND, U3.COIL1
  N1: IC3.IN, IC4.IN, U2.GND, S3.Pin_3, S3.Pin_4, U3.COIL2
  N2: IC3.OUT, U2.VCC, U2.CH_PD
  N3: U2.GPIO_0, U3.MAIN
  N4: U2.REST, S3.Pin_1, S3.Pin_2

notes:
  Solenoid Valve
  YL98 Module
