# Fritzing sketch Temp-Photores (saved by Fritzing 0.9.3b)
breadboards: 1

parts:
  IC7 = Voltage Regulator [package=to220-igo]
  IC8 = Voltage Regulator [package=to220-igo]
  U7 = ESP8266 WiFi Module [part_number=ESP8266]
  S5 = Pushbutton [package="[THT]"]
  R1 = Resistor [tolerance=±5% resistance=10k package=THT]
  R2 = PHOTOCELL [package=photocell]
  T1 = LM35 Temperature Sensor [package="TO92 [THT]"]
  T2 = LM35 Temperature Sensor [package="TO92 [THT]"]
  U8 = ESP8266 WiFi Module [part_number=ESP8266]  # not connected

nets:
  GND: IC7.GND, IC8.GND
  GND_2: IC7.IN, IC8.IN, U7.GND, S5.Pin_3, S5.Pin_4, R1.Pin_1, T1.GND, T2.GND
  N1: IC7.OUT, R2.P$1, T1.+Vs, T2.+Vs
  N2: IC8.OUT, U7.VCC, U7.CH_PD
  N3: U7.GPIO_0, T1.Vout
  N4: U7.GPIO_2, T2.Vout
  N5: U7.GPIO_5, R1.Pin_0, R2.P$2
  N6: U7.REST, S5.Pin_1, S5.Pin_2
